# Fritzing sketch arduino_ethernet_rfid (saved by Fritzing 0.9.2b)
breadboards: 1

parts:
  Part1 = Arduino Uno (Rev3)
  Part3 = RFID-RC522-v2
  R1 = Resistor [tolerance=±5% resistance=330 package="0805 [SMD]"]
  R2 = Resistor [tolerance=±5% resistance=330 package="0805 [SMD]"]
  LED1 = LED - 3mm [color="Red (633nm)" package="3 mm [THT]"]
  LED2 = LED - 3mm [color="Green (560nm)" package="3 mm [THT]"]
  Part4 = Arduino Ethernet Shield (Rev3)  # not connected

nets:
  N1: Part1.D8, Part3.RST
  N2: Part1.D9_PWM, Part3.SDA
  N3: Part1.D11_PWM/MOSI, Part3.MOSI
  N4: Part1.D12/MISO, Part3.MISO
  N5: Part1.D13/SCK, Part3.SCK
  N6: Part1.D3_PWM, R2.Pin_1
  N7: Part1.D4, R1.Pin_1
  N8: Part1.3V3, Part3.3_3V
  GND: Part1.GND, Part3.GND, LED1.cathode, LED2.cathode
  N9: R1.Pin_0, LED2.anode
  N10: R2.Pin_0, LED1.anode

custom parts:
  RFID-RC522-v2: A simple China made RFID-RC522 Reader; do check the pin labels, as this is a MFRC522 based clone.
